// Digital circuit MIPS.dig as structural Verilog
module MIPS (
  input  CLK
);

  wire add_2_s, and_1_out, and_2_out, multiplexer_1_out, multiplexer_3_out, multiplexer_5_out,
       multiplexer_6_out, multiplexer_7_out, or_1_out, ramdualport_1_d, registradores_1_p1,
       registradores_1_p7, ula_1_p5, undriven;
  wire [1:0] ula_1_p4;
  wire [15:0] bitextender_2_out, bitextender_3_out;
  wire [31:0] multiplexer_2_out, multiplexer_4_out, PC_q, registradores_1_p8;
  wire [31:2] bitextender_1_out;
  wire [31:16] \Memória_de_Instrução_d , registradores_1_p5;

  Add add (.a(PC_q[0]), .b(1'b0), .c_i(1'b0));  // open: s, c_o
  Register PC (.D(multiplexer_6_out), .C(CLK), .en(1'b1), .Q(PC_q[0]));
  ROM \Memória_de_Instrução  (.A(PC_q[1:0]), .sel(1'b1), .D(\Memória_de_Instrução_d [16]));
  ROM #(.Bits(6)) Unidade_de_Controle (.A(registradores_1_p5[27:26]), .sel(1'b1));  // open: D
  Multiplexer multiplexer_1 (
    .in_0(\Memória_de_Instrução_d [27]), .in_1(registradores_1_p5[16]), .out(multiplexer_1_out));  // open: sel
  Add add_2 (.a(PC_q[0]), .b(1'b0), .c_i(1'b0), .s(add_2_s));  // open: c_o
  BitExtender #(.inputBits(16), .outputBits(30)) bitextender_1 (.in(\Memória_de_Instrução_d ), .out(bitextender_1_out));
  BitExtender #(.inputBits(16)) bitextender_2 (.in(\Memória_de_Instrução_d ), .out(bitextender_2_out));
  BitExtender bitextender_3 (.in(\Memória_de_Instrução_d [23:16]), .out(bitextender_3_out));
  // registradores registradores_1: pin names not known; wires that end beside it: registradores_1_p1, CLK, multiplexer_1_out, registradores_1_p5[25:21], registradores_1_p5[20:16], add_2_s, registradores_1_p7, registradores_1_p8
  Multiplexer multiplexer_2 (
    .in_0(bitextender_2_out[0]), .in_1(bitextender_3_out[0]), .out(multiplexer_2_out[0]));  // open: sel
  Multiplexer multiplexer_3 (.in_0(registradores_1_p7), .in_1(1'b0), .out(multiplexer_3_out));  // open: sel
  Multiplexer #(.Bits(32)) multiplexer_4 (
    .in_0(registradores_1_p8), .in_1(multiplexer_2_out), .out(multiplexer_4_out));  // open: sel
  and and_1 (and_1_out, undriven, ula_1_p5);
  // ULA ula_1: pin names not known; wires that end beside it: registradores_1_p7, multiplexer_4_out, \Memória_de_Instrução_d [26:22], ula_1_p4, ula_1_p5
  Multiplexer multiplexer_5 (.sel(or_1_out), .in_0(multiplexer_3_out), .in_1(1'b0), .out(multiplexer_5_out));
  or or_1 (or_1_out, and_1_out, and_2_out);
  and and_2 (and_2_out, undriven, ~ula_1_p5);  // And
  Multiplexer multiplexer_6 (.in_0(multiplexer_5_out), .out(multiplexer_6_out));  // open: sel, in_1
  RAMDualPort ramdualport_1 (.A(ula_1_p4), .Din(registradores_1_p8[0]), .C(CLK), .D(ramdualport_1_d));  // open: str, ld
  Multiplexer multiplexer_7 (.in_0(ula_1_p4[0]), .in_1(ramdualport_1_d), .out(multiplexer_7_out));  // open: sel
  Multiplexer multiplexer_8 (.in_0(multiplexer_7_out), .in_1(1'b0), .out(registradores_1_p1));  // open: sel
  // Pins of 1 and 32 bits meet at registradores_1_p8
  // Pins of 1 and 32 bits meet at multiplexer_2_out
  // Pins of 1 and 5 bits meet at \Memória_de_Instrução_d [31:27]
  // Pins of 1 and 5 bits meet at registradores_1_p5[20:16]
  // Pins of 1 and 32 bits meet at {registradores_1_p5, \Memória_de_Instrução_d }
  // Pins of 2 and 6 bits meet at registradores_1_p5[31:26]
  // Pins of 8 and 16 bits meet at \Memória_de_Instrução_d 
  // Pins of 1 and 2 and 32 bits meet at PC_q
  // Pins of 1 and 16 bits meet at bitextender_2_out
  // Pins of 1 and 4 bits meet at 4'b0100
  // Pins of 1 and 4 bits meet at 4'b0100
  // Pins of 1 and 32 bits meet at {bitextender_1_out, 2'b00}

  // Notes on the sheet:
  //   para o "and imm" e "imm"
  //   sem sinal
  //   com sinal
  //   JumpAddr
  //   BranchAdder
  //   branches
  //   para o "imm" não estendido
  //   para o "load upper imm"
endmodule
