// Digital circuit unidadeLogicaAritmetica.dig as structural Verilog
module unidadeLogicaAritmetica (
  input  [31:0] A,
  input  [31:0] B,
  input  [2:0] OP,
  output [31:0] S,
  output Z
);

  wire [0:0] comparator_1_lt;
  wire [31:0] add_1_s, and_1_out, nor_1_out, not_1_out, or_1_out, sub_1_s;
  wire [63:0] mul_1_mul;

  Add #(.Bits(32)) add_1 (.a(A), .b(B), .c_i(1'b0), .s(add_1_s));  // open: c_o
  Sub #(.Bits(32)) sub_1 (.a(A), .b(B), .c_i(1'b0), .s(sub_1_s));  // open: c_o
  Mul #(.Bits(32)) mul_1 (.a(A), .b(B), .mul(mul_1_mul));
  assign and_1_out = A & B;  // And and_1, 32 bits wide
  assign or_1_out = A | B;  // Or or_1, 32 bits wide
  assign nor_1_out = ~(A | B);  // NOr nor_1, 32 bits wide
  Comparator #(.Bits(32)) comparator_1 (.a(A), .b(B), .lt(comparator_1_lt[0]));  // open: gt, eq
  assign not_1_out = ~A;  // Not not_1, 32 bits wide
  Multiplexer #(.Selector_Bits(3), .Bits(32)) multiplexer_1 (
    .sel(OP), .in_0(add_1_s), .in_1(sub_1_s), .in_2(mul_1_mul[31:0]), .in_3(and_1_out), .in_4(or_1_out),
    .in_5(nor_1_out), .in_6({{31{1'b0}}, comparator_1_lt[0]}), .in_7(not_1_out), .out(S));
  Comparator #(.Bits(32)) comparator_2 (.a(S), .b({32{1'b0}}), .eq(Z));  // open: gt, lt
endmodule
