// Digital circuit MICO12.dig as structural Verilog
module MICO12 (
  input  clk
);

  wire and_1_out, unidadelogicaaritmetica_1_z;
  wire [1:0] rom_2_d_2;
  wire [13:0] rom_2_d;
  wire [15:0] add_1_s, blocoderegistradores_1_a_2, IP_q, multiplexer_1_out, multiplexer_2_out, ROM_d;
  wire [23:0] unidadelogicaaritmetica_1_s;
  wire [31:0] bitextender_1_out, blocoderegistradores_1_b_2, multiplexer_3_out, multiplexer_4_out,
       multiplexer_5_out, ramdualport_1_d;
  wire [31:16] blocoderegistradores_1_a_2_2, ROM_d_2;
  wire [31:24] unidadelogicaaritmetica_1_s_2;

  Add #(.Bits(16)) add_1 (.a(IP_q), .b(16'h1), .c_i(1'b0), .s(add_1_s));  // open: c_o
  Multiplexer #(.Bits(16)) multiplexer_1 (
    .sel(and_1_out), .in_0(multiplexer_2_out), .in_1(ROM_d), .out(multiplexer_1_out));
  Register #(.Bits(16)) IP (.D(multiplexer_1_out), .C(clk), .en(rom_2_d[13]), .Q(IP_q));
  Multiplexer #(.Selector_Bits(2), .Bits(16)) multiplexer_2 (
    .sel(rom_2_d_2), .in_0(add_1_s), .in_1(blocoderegistradores_1_a_2), .in_2(ROM_d), .in_3({16{1'b0}}),
    .out(multiplexer_2_out));
  ROM #(.AddrBits(16), .Bits(32)) ROM (.A(IP_q), .sel(1'b1), .D({ROM_d_2, ROM_d}));
  and and_1 (and_1_out, unidadelogicaaritmetica_1_z, rom_2_d[1]);
  BitExtender #(.inputBits(16), .outputBits(32)) bitextender_1 (.in(ROM_d), .out(bitextender_1_out));
  blocoDeRegistradores blocoderegistradores_1 (
    .C(multiplexer_5_out), .c_2(ROM_d_2[19:16]), .clk(clk), .a(ROM_d_2[27:24]), .b(ROM_d_2[23:20]),
    .w(rom_2_d[12]), .A_2({blocoderegistradores_1_a_2_2, blocoderegistradores_1_a_2}),
    .B_2(blocoderegistradores_1_b_2));
  ROM #(.AddrBits(4), .Bits(14)) rom_2 (.A(ROM_d_2[31:28]), .sel(1'b1), .D({rom_2_d[13:4], rom_2_d_2, rom_2_d[1:0]}));
  Multiplexer #(.Bits(32)) multiplexer_3 (
    .sel(rom_2_d[0]), .in_0({32{1'b0}}), .in_1({blocoderegistradores_1_a_2_2, blocoderegistradores_1_a_2}),
    .out(multiplexer_3_out));
  Multiplexer #(.Bits(32)) multiplexer_4 (
    .sel(rom_2_d[11]), .in_0(blocoderegistradores_1_b_2), .in_1(bitextender_1_out), .out(multiplexer_4_out));
  // Probe on multiplexer_3_out
  unidadeLogicaAritmetica unidadelogicaaritmetica_1 (
    .A({blocoderegistradores_1_a_2_2, blocoderegistradores_1_a_2}), .B(multiplexer_4_out),
    .OP(rom_2_d[10:8]), .S({unidadelogicaaritmetica_1_s_2, unidadelogicaaritmetica_1_s}),
    .Z(unidadelogicaaritmetica_1_z));
  Multiplexer #(.Selector_Bits(2), .Bits(32)) multiplexer_5 (
    .sel(rom_2_d[5:4]), .in_0({unidadelogicaaritmetica_1_s_2, unidadelogicaaritmetica_1_s}),
    .in_1(ramdualport_1_d), .in_2({{16{1'b0}}, add_1_s}), .in_3({32{1'b0}}), .out(multiplexer_5_out));
  RAMDualPort #(.AddrBits(24), .Bits(32)) ramdualport_1 (
    .A(unidadelogicaaritmetica_1_s), .Din(blocoderegistradores_1_b_2), .str(rom_2_d[7]), .C(clk),
    .ld(rom_2_d[6]), .D(ramdualport_1_d));
  // Pins of 1 and 4 bits meet at 4'b0100

  // Notes on the sheet:
  //   contents of ROM (hex, n*v repeats v):
  //   82010,81020,1230,b3000,13240,b4000,21450,b5000,31360,b6000,41370
  //   ,91370,51380,b8000,61390,b9000,740a0,ba000,a2900,92080,b8000,e1200
  //   ,81010,c0000,8b0b0,e2300,82020,db000,e6500,86060,cc000,bc000,f0000
  //   contents of rom_2 (hex, n*v repeats v):
  //   3000,3100,3200,3300,3400,3500,3600,3800,3800,2850,2080,2001,3008
  //   ,2004,2102
endmodule
