// Digital circuit MIPS.dig as structural Verilog
module MIPS (
  input  CLK
);

  wire and_1_out, and_2_out, or_1_out, or_2_out, ULA_z;
  wire [3:0] PC_q_2;
  wire [4:0] \Memória_de_Instrução_d_2 , multiplexer_1_out;
  wire [11:0] Unidade_de_Controle_d;
  wire [19:0] PC_q;
  wire [23:0] add_2_s, multiplexer_3_out, multiplexer_5_out, multiplexer_6_out;
  wire [23:2] bitextender_1_out;
  wire [31:0] bitextender_2_out, bitextender_3_out, bitextender_4_out, multiplexer_2_out, multiplexer_4_out,
       multiplexer_7_out, multiplexer_8_out, ramdualport_1_d, registradores_1_a, registradores_1_b, ULA_s;
  wire [31:16] \Memória_de_Instrução_d , \Memória_de_Instrução_d_3 ;

  Add #(.Bits(24)) add (.a({PC_q_2, PC_q}), .b(24'h4), .c_i(1'b0));  // open: s, c_o
  Register #(.Bits(24)) PC (.D(multiplexer_6_out), .C(CLK), .en(1'b1), .Q({PC_q_2, PC_q}));
  ROM #(.AddrBits(24), .Bits(32)) \Memória_de_Instrução  (
    .A({PC_q_2, PC_q}), .sel(1'b1),
    .D({\Memória_de_Instrução_d_3 , \Memória_de_Instrução_d [31:27], \Memória_de_Instrução_d_2 , \Memória_de_Instrução_d [21:16]}));
  ROM #(.AddrBits(5), .Bits(12)) Unidade_de_Controle (
    .A(\Memória_de_Instrução_d_3 [30:26]), .sel(1'b1), .D(Unidade_de_Controle_d));
  BitExtender #(.inputBits(16), .outputBits(22)) bitextender_1 (
    .in({\Memória_de_Instrução_d [31:27], \Memória_de_Instrução_d_2 , \Memória_de_Instrução_d [21:16]}),
    .out(bitextender_1_out));
  Multiplexer #(.Bits(5)) multiplexer_1 (
    .sel(Unidade_de_Controle_d[5]), .in_0(\Memória_de_Instrução_d [31:27]),
    .in_1(\Memória_de_Instrução_d_3 [20:16]), .out(multiplexer_1_out));
  Add #(.Bits(24)) add_2 (.a({PC_q_2, PC_q}), .b(24'h4), .c_i(1'b0), .s(add_2_s));  // open: c_o
  BitExtender #(.inputBits(24), .outputBits(32)) bitextender_2 (.in(add_2_s), .out(bitextender_2_out));
  BitExtender #(.inputBits(16), .outputBits(32)) bitextender_3 (
    .in({\Memória_de_Instrução_d [31:27], \Memória_de_Instrução_d_2 , \Memória_de_Instrução_d [21:16]}),
    .out(bitextender_3_out));
  BitExtender #(.inputBits(16), .outputBits(32)) bitextender_4 (
    .in({\Memória_de_Instrução_d [31:27], \Memória_de_Instrução_d_2 , \Memória_de_Instrução_d [21:16]}),
    .out(bitextender_4_out));
  registradores registradores_1 (
    .D(multiplexer_8_out), .clk(CLK), .write_enable(Unidade_de_Controle_d[11]),
    .write_register(multiplexer_1_out), .RA(\Memória_de_Instrução_d_3 [25:21]),
    .RB(\Memória_de_Instrução_d_3 [20:16]), .R31_IN(bitextender_2_out), .LINK(Unidade_de_Controle_d[0]),
    .A(registradores_1_a), .B(registradores_1_b));
  Multiplexer #(.Bits(32)) multiplexer_2 (
    .sel(Unidade_de_Controle_d[2]), .in_0(bitextender_3_out), .in_1(bitextender_4_out),
    .out(multiplexer_2_out));
  Multiplexer #(.Bits(24)) multiplexer_3 (
    .sel(Unidade_de_Controle_d[0]), .in_0(registradores_1_a[23:0]),
    .in_1({\Memória_de_Instrução_d_3 [21:16], \Memória_de_Instrução_d [31:27], \Memória_de_Instrução_d_2 , \Memória_de_Instrução_d [21:16], 2'b00}),
    .out(multiplexer_3_out));
  Multiplexer #(.Bits(32)) multiplexer_4 (
    .sel(Unidade_de_Controle_d[5]), .in_0(registradores_1_b), .in_1(multiplexer_2_out),
    .out(multiplexer_4_out));
  and and_1 (and_1_out, Unidade_de_Controle_d[4], ULA_z);
  ULA ULA (
    .A(registradores_1_a), .B(multiplexer_4_out), .OP(Unidade_de_Controle_d[10:8]),
    .shamt({1'b0, \Memória_de_Instrução_d_2 }), .S(ULA_s), .Z(ULA_z));
  Multiplexer #(.Bits(24)) multiplexer_5 (
    .sel(or_1_out), .in_0(multiplexer_3_out), .in_1({bitextender_1_out, 2'b00}), .out(multiplexer_5_out));
  or or_1 (or_1_out, and_1_out, and_2_out);
  and and_2 (and_2_out, Unidade_de_Controle_d[4], ~ULA_z);  // And
  RAMDualPort #(.AddrBits(24), .Bits(32)) ramdualport_1 (
    .A(ULA_s[23:0]), .Din(registradores_1_b), .str(Unidade_de_Controle_d[7]), .C(CLK),
    .ld(Unidade_de_Controle_d[6]), .D(ramdualport_1_d));
  Multiplexer #(.Bits(24)) multiplexer_6 (
    .sel(or_2_out), .in_0(multiplexer_5_out), .in_1({PC_q_2, PC_q}), .out(multiplexer_6_out));
  or or_2 (or_2_out, Unidade_de_Controle_d[3], Unidade_de_Controle_d[4]);
  Multiplexer #(.Bits(32)) multiplexer_7 (
    .sel(Unidade_de_Controle_d[6]), .in_0(ULA_s), .in_1(ramdualport_1_d), .out(multiplexer_7_out));
  Multiplexer #(.Bits(32)) multiplexer_8 (
    .sel(Unidade_de_Controle_d[1]), .in_0(multiplexer_7_out),
    .in_1({\Memória_de_Instrução_d [31:27], \Memória_de_Instrução_d_2 , \Memória_de_Instrução_d [21:16], {16{1'b0}}}),
    .out(multiplexer_8_out));

  // Notes on the sheet:
  //   contents of Unidade_de_Controle (hex, n*v repeats v):
  //   0,20,0,24
  //   PC+4
  //   para o "and imm" e "imm"
  //   com sinal
  //   sem sinal
  //   JumpAddr
  //   BranchAdder
  //   branches
  //   para o "imm" não estendido
  //   para o "load upper imm"
endmodule
