// Digital circuit ULA.dig as structural Verilog
module ULA (
  input  [31:0] A,
  input  [31:0] B,
  input  [2:0] OP,
  input  [5:0] shamt,
  output [31:0] S,
  output Z
);

  wire [0:0] comparator_lt;
  wire [31:0] add_s, and_1_out, nor_1_out, or_1_out, shift_left_out, shift_right_out, sub_s;

  Add #(.Bits(32)) add (.a(A), .b(B), .c_i(1'b0), .s(add_s));  // open: c_o
  Sub #(.Bits(32)) sub (.a(A), .b(B), .c_i(1'b0), .s(sub_s));  // open: c_o
  assign and_1_out = A & B;  // And and_1, 32 bits wide
  assign or_1_out = A | B;  // Or or_1, 32 bits wide
  assign nor_1_out = ~(A | B);  // NOr nor_1, 32 bits wide
  Comparator #(.Bits(32)) comparator (.a(A), .b(B), .lt(comparator_lt[0]));  // open: gt, eq
  BarrelShifter #(.Bits(32)) shift_left (.in(A), .shift({1'b0, shamt[4:0]}), .out(shift_left_out));
  BarrelShifter #(.Bits(32), .direction("right")) shift_right (
    .in(A), .shift({1'b0, shamt[4:0]}), .out(shift_right_out));
  Multiplexer #(.Selector_Bits(3), .Bits(32)) multiplexer_1 (
    .sel(OP), .in_0(add_s), .in_1(sub_s), .in_2(and_1_out), .in_3(or_1_out), .in_4(nor_1_out),
    .in_5({{31{1'b0}}, comparator_lt[0]}), .in_6(shift_left_out), .in_7(shift_right_out),
    .out({S[31:10], S[10], S[8:6], S[6], S[4:0]}));
  nor nor_2 (Z, S[0], S[1], S[2], S[3], S[4], S[6], S[6], S[7], S[8], S[10], S[10], S[11], S[12], S[13], S[14], S[15], S[16], S[17], S[18], S[19], S[20], S[21], S[22], S[23], S[24], S[25], S[26], S[27], S[28], S[29], S[30], S[31]);
  // Pins of 5 and 6 bits meet at shamt

  assign {S[9], S[5]} = {S[10], S[6]};
endmodule
